// Logisim project Lab4.circ as structural Verilog: 1 circuit, main circuit main
module main (
  input  a,
  input  b,
  input  c
);

  wire ab_out, ac_out, or_1_out;

  and ab (ab_out, b, a);
  LED led_1 (.in(ab_out));
  and ac (ac_out, c, a);
  or or_1 (or_1_out, ab_out, ac_out);
  LED led_2 (.in(or_1_out));

  // Notes on the sheet:
  //   B
  //   A
  //   ab + ac
endmodule
