// Logisim project 1_bit_Full_Adder.circ as structural Verilog: 1 circuit, main circuit main
module main (
  input  A,
  input  B,
  input  Cin
);

  wire nand_1_out, nand_2_out, nand_3_out, nand_4_out, nand_5_out, nand_6_out, nand_7_out, nand_8_out,
       nand_9_out, not_1_out, not_2_out, not_3_out;

  not not_1 (not_1_out, A);
  not not_2 (not_2_out, B);
  not not_3 (not_3_out, Cin);
  nand nand_1 (nand_1_out, A, not_2_out, not_3_out);
  nand nand_2 (nand_2_out, not_1_out, not_2_out, Cin);
  nand nand_3 (nand_3_out, A, B, Cin);
  nand nand_4 (nand_4_out, nand_1_out, nand_2_out, nand_3_out, nand_5_out);
  LED led_1 (.in(nand_4_out));
  nand nand_5 (nand_5_out, not_1_out, B, not_3_out);
  nand nand_6 (nand_6_out, A, Cin);
  nand nand_7 (nand_7_out, A, B);
  nand nand_8 (nand_8_out, nand_6_out, nand_7_out, nand_9_out);
  LED led_2 (.in(nand_8_out));
  nand nand_9 (nand_9_out, B, Cin);

  // Notes on the sheet:
  //   Sum
  //   Carry
endmodule
