// Logisim project 1_bit_Half_Adder.circ as structural Verilog: 1 circuit, main circuit main
module main (
  input  A,
  input  B
);

  wire and_1_out, xor_1_out;

  xor xor_1 (xor_1_out, B, A);
  LED led_1 (.in(xor_1_out));
  and and_1 (and_1_out, B, A);
  LED led_2 (.in(and_1_out));

  // Notes on the sheet:
  //   Sum
  //   Carry
endmodule
