// Logisim project 4_bit_Chained_Adder.circ as structural Verilog: 1 circuit, main circuit main
module main (
  input  A0,
  input  A1,
  input  A2,
  input  A3,
  input  B0,
  input  B1,
  input  B2,
  input  B3,
  input  Cin
);

  wire nand_1_out, nand_2_out, nand_3_out, nand_4_out, nand_5_out, nand_6_out, nand_7_out, nand_8_out,
       nand_9_out, nand_10_out, nand_11_out, nand_12_out, nand_13_out, nand_14_out, nand_15_out, nand_16_out,
       nand_17_out, nand_18_out, nand_19_out, nand_20_out, nand_21_out, nand_22_out, nand_23_out,
       nand_24_out, nand_25_out, nand_26_out, nand_27_out, nand_28_out, nand_29_out, nand_30_out,
       nand_31_out, nand_32_out, nand_33_out, nand_34_out, nand_35_out, nand_36_out, not_1_out, not_2_out,
       not_3_out, not_4_out, not_5_out, not_6_out, not_7_out, not_8_out, not_9_out, not_10_out, not_11_out,
       not_12_out;

  not not_1 (not_1_out, A0);
  not not_2 (not_2_out, B0);
  not not_3 (not_3_out, Cin);
  nand nand_1 (nand_1_out, A0, not_2_out, not_3_out);
  nand nand_2 (nand_2_out, not_1_out, not_2_out, Cin);
  nand nand_3 (nand_3_out, A0, B0, Cin);
  nand nand_4 (nand_4_out, nand_1_out, nand_2_out, nand_3_out, nand_5_out);
  LED led_1 (.in(nand_4_out));
  nand nand_5 (nand_5_out, not_1_out, B0, not_3_out);
  nand nand_6 (nand_6_out, A0, Cin);
  nand nand_7 (nand_7_out, A0, B0);
  nand nand_8 (nand_8_out, nand_6_out, nand_7_out, nand_9_out);
  nand nand_9 (nand_9_out, B0, Cin);
  not not_4 (not_4_out, A1);
  not not_5 (not_5_out, B1);
  not not_6 (not_6_out, nand_8_out);
  nand nand_10 (nand_10_out, A1, not_5_out, not_6_out);
  nand nand_11 (nand_11_out, not_4_out, not_5_out, nand_8_out);
  nand nand_12 (nand_12_out, A1, B1, nand_8_out);
  nand nand_13 (nand_13_out, nand_10_out, nand_11_out, nand_12_out, nand_14_out);
  LED led_2 (.in(nand_13_out));
  nand nand_14 (nand_14_out, not_4_out, B1, not_6_out);
  nand nand_15 (nand_15_out, A1, nand_8_out);
  nand nand_16 (nand_16_out, A1, B1);
  nand nand_17 (nand_17_out, nand_15_out, nand_16_out, nand_18_out);
  nand nand_18 (nand_18_out, B1, nand_8_out);
  not not_7 (not_7_out, A2);
  not not_8 (not_8_out, B2);
  not not_9 (not_9_out, nand_17_out);
  nand nand_19 (nand_19_out, A2, not_8_out, not_9_out);
  nand nand_20 (nand_20_out, not_7_out, not_8_out, nand_17_out);
  nand nand_21 (nand_21_out, A2, B2, nand_17_out);
  nand nand_22 (nand_22_out, nand_19_out, nand_20_out, nand_21_out, nand_23_out);
  LED led_3 (.in(nand_22_out));
  nand nand_23 (nand_23_out, not_7_out, B2, not_9_out);
  nand nand_24 (nand_24_out, A2, nand_17_out);
  nand nand_25 (nand_25_out, A2, B2);
  nand nand_26 (nand_26_out, nand_24_out, nand_25_out, nand_27_out);
  nand nand_27 (nand_27_out, B2, nand_17_out);
  not not_10 (not_10_out, A3);
  not not_11 (not_11_out, B3);
  not not_12 (not_12_out, nand_26_out);
  nand nand_28 (nand_28_out, A3, not_11_out, not_12_out);
  nand nand_29 (nand_29_out, not_10_out, not_11_out, nand_26_out);
  nand nand_30 (nand_30_out, nand_28_out, nand_29_out, nand_31_out, nand_32_out);
  LED led_4 (.in(nand_30_out));
  nand nand_31 (nand_31_out, A3, B3, nand_26_out);
  nand nand_32 (nand_32_out, not_10_out, B3, not_12_out);
  nand nand_33 (nand_33_out, A3, nand_26_out);
  nand nand_34 (nand_34_out, A3, B3);
  nand nand_35 (nand_35_out, nand_33_out, nand_34_out, nand_36_out);
  LED led_5 (.in(nand_35_out));
  nand nand_36 (nand_36_out, B3, nand_26_out);

  // Notes on the sheet:
  //   A - 1001
  //   B - 1011
  //   C0
  //   C1
  //   C2
  //   C3
  //   C - Output = [1]0100
  //   Carry (Overflow)
endmodule
