// Logisim project Lab6_0_5_Counter.circ as structural Verilog: 1 circuit, main circuit main
module main (
);

  wire A_qn, and_1_out, and_2_out, clock_1_out;
  wire [2:0] C_q;

  Clock clock_1 (.out(clock_1_out));
  J_K_Flip_Flop A (.J(and_1_out), .K(C_q[0]), .clk(clock_1_out), .Q(C_q[2]), .Qn(A_qn));  // open: preset, reset
  and and_1 (and_1_out, C_q[1], C_q[0]);
  and and_2 (and_2_out, A_qn, C_q[0]);
  J_K_Flip_Flop B (.J(and_2_out), .K(C_q[0]), .clk(clock_1_out), .Q(C_q[1]));  // open: Qn, preset, reset
  J_K_Flip_Flop C (.J(1'b1), .K(1'b1), .clk(clock_1_out), .Q(C_q[0]));  // open: Qn, preset, reset
  Hex_Digit_Display hex_digit_display_1 (.value({1'b0, C_q}));  // open: dp
endmodule
