// Logisim project Lab6_Counter.circ as structural Verilog: 1 circuit, main circuit main
module main (
);

  wire A_qn, and_1_out, and_2_out, and_3_out, and_4_out, and_5_out, and_6_out, and_7_out, and_8_out, C_qn,
       clock_1_out, D_qn, or_1_out, or_2_out, or_3_out, or_4_out;
  wire [3:0] D_q;

  Clock clock_1 (.out(clock_1_out));
  and and_1 (and_1_out, D_qn, D_q[1]);
  and and_2 (and_2_out, A_qn, D_q[2], D_q[1], D_q[0]);
  or or_1 (or_1_out, and_3_out, and_4_out);
  or or_2 (or_2_out, and_5_out, and_6_out);
  or or_3 (or_3_out, and_7_out, and_8_out);
  or or_4 (or_4_out, A_qn, D_q[0], C_qn);
  J_K_Flip_Flop A (.J(and_2_out), .K(and_1_out), .clk(clock_1_out), .Q(D_q[3]), .Qn(A_qn));  // open: preset, reset
  and and_3 (and_3_out, A_qn, D_q[1], D_q[0]);
  and and_4 (and_4_out, D_q[2], D_q[1]);
  and and_5 (and_5_out, C_qn, D_q[0]);
  and and_6 (and_6_out, D_q[3], D_q[2], C_qn);
  and and_7 (and_7_out, D_q[3], D_q[1]);
  and and_8 (and_8_out, D_q[1], D_q[0]);
  Hex_Digit_Display hex_digit_display_1 (.value(D_q));  // open: dp
  J_K_Flip_Flop B (.J(or_1_out), .K(and_3_out), .clk(clock_1_out), .Q(D_q[2]));  // open: Qn, preset, reset
  J_K_Flip_Flop C (.J(or_2_out), .K(or_3_out), .clk(clock_1_out), .Q(D_q[1]), .Qn(C_qn));  // open: preset, reset
  J_K_Flip_Flop D (.J(or_4_out), .K(1'b1), .clk(clock_1_out), .Q(D_q[0]), .Qn(D_qn));  // open: preset, reset

  // Notes on the sheet:
  //   A'BCD
  //   A'CD+BC
  //   C'D+ABC'
  //   AC+DC
  //   A'+D+C'
  //   CD'
endmodule
