// Logisim project Lab6_Counter_Optimized.circ as structural Verilog: 1 circuit, main circuit main
module main (
);

  wire A_qn, and_1_out, and_2_out, C_qn, clock_1_out, or_1_out, or_2_out;
  wire [3:0] D_q;

  Clock clock_1 (.out(clock_1_out));
  and and_1 (and_1_out, D_q[2], D_q[1], D_q[0]);
  J_K_Flip_Flop A (.J(and_1_out), .K(D_q[1]), .clk(clock_1_out), .Q(D_q[3]), .Qn(A_qn));  // open: preset, reset
  or or_1 (or_1_out, D_q[3], D_q[0]);
  or or_2 (or_2_out, A_qn, C_qn);
  and and_2 (and_2_out, D_q[1], D_q[0]);
  J_K_Flip_Flop B (.J(and_2_out), .K(and_2_out), .clk(clock_1_out), .Q(D_q[2]));  // open: Qn, preset, reset
  J_K_Flip_Flop C (.J(D_q[0]), .K(or_1_out), .clk(clock_1_out), .Q(D_q[1]), .Qn(C_qn));  // open: preset, reset
  J_K_Flip_Flop D (.J(or_2_out), .K(1'b1), .clk(clock_1_out), .Q(D_q[0]));  // open: Qn, preset, reset
  Hex_Digit_Display hex_digit_display_1 (.value(D_q));  // open: dp
endmodule
