// Logisim project Lab6_RS_FlipFlop.circ as structural Verilog: 1 circuit, main circuit main
module main (
  input  R,
  input  S
);

  wire nor_1_out, nor_2_out;

  nor nor_1 (nor_1_out, R, nor_2_out);
  nor nor_2 (nor_2_out, nor_1_out, S);
  LED Q (.in(nor_1_out));
  LED Q_prime (.in(nor_2_out));
endmodule
